# Fritzing sketch motion_controller (saved by Fritzing 0.9.2b)

parts:
  GY1 = MPU-6050 Board GY-521 [form="♀ (female)" package=THT]
  U1 = NodeMCU V1.0
  S1 = Pushbutton [package="[THT]"]
  R1 = Resistor [tolerance=±5% resistance=10k package=THT]

nets:
  N1: GY1.pin1, U1.3V3, S1.Pin_1
  N2: GY1.pin2, U1.GND, R1.Pin_1
  N3: GY1.pin3, U1.D1
  N4: GY1.pin4, U1.D2
  N5: GY1.pin8, U1.D7
  N6: U1.D6, S1.Pin_3, S1.Pin_4, R1.Pin_0

custom parts:
  MPU-6050 Board GY-521: Acelerometro y Giroscopio MPU-6050 Board GY-521
  NodeMCU V1.0: ESP8266 based NodeMCU
